# Fritzing sketch Untitled Sketch 2 (saved by Fritzing 0.9.2b)
perfboards: 1

parts:
  XTAL1 = Crystal [frequency="16 Mhz" package=THT]
  U1 = ATmega 328P [package=dip]
  J1 = female pin header, 4 pins [form="♀ (female)"]
  R1 = Resistor [tolerance=±5% resistance=68 package=THT]
  J2 = female pin header, 8 pins [form="♀ (female)"]
  J3 = female pin header, 8 pins [form="♀ (female)"]
  C3 = Ceramic Capacitor [package="100 mil [THT, multilayer]"]
  C4 = Ceramic Capacitor [package="100 mil [THT, multilayer]"]
  J4 = female pin header, 8 pins [form="♀ (female)"]
  J5 = female pin header, 8 pins [form="♀ (female)"]
  R3 = Resistor [tolerance=±5% resistance=10k package=THT]
  J7 = female pin header, 3 pins [form="♀ (female)"]
  J6 = female pin header, 3 pins [form="♀ (female)"]
  R4 = Resistor [tolerance=±5% resistance=68 package=THT]
  R5 = Resistor [tolerance=±5% resistance=2.2k package=THT]
  D1 = Rectifier Diode [part_number=1N4001 package="300 mil [THT]"]
  D2 = Rectifier Diode [part_number=1N4001 package="300 mil [THT]"]
  J8 = female pin header, 4 pins [form="♀ (female)"]
  J9 = female pin header, 4 pins [form="♀ (female)"]
  U2 = Voltage Regulator - 5V [package="TO220 [THT]"]
  C5 = Electrolytic Capacitor [capacitance=10µF package="100 mil [THT, electrolytic]"]
  C6 = Electrolytic Capacitor [capacitance=10µF package="100 mil [THT, electrolytic]"]

nets:
  N1: XTAL1.pin_0, C3.1
  N2: U1.PC6_(PCINT14/^RESET)_[RESET], R3.Pin_1, J6.pin3
  N3: U1.PD0_(PCINT16/RXD)_[D0], J6.pin2
  N4: U1.PD1_(PCINT17/TXD)_[D1], J6.pin1
  N5: U1.PD2_(PCINT18/INT0)_[D2], R1.Pin_1
  N6: U1.PD4_(PCINT20/XCK/T0)_[D4], R4.Pin_1
  N7: U1.VCC, J5.pin8
  N8: U1.GND#7, J2.pin6
  N9: U1.PB6_(PCINT6/XTAL1/TOSC1)_[XTAL1], C4.1
  N10: U1.PD5_(PCINT21/OC0B/T1)_[D5_PWM], R5.Pin_1
  N11: U1.PB1_(OC1A/PCINT1)_[D9_PWM], J9.pin2
  N12: U1.PB2_(^SS/OC1B/PCINT2)_[D10_PWM], J8.pin2
  N13: U1.PB3_(MOSI/OC2A/PCINT3)_[D11_PWM], J7.pin1, J8.pin3
  N14: U1.PB4_(MISO/PCINT4)_[D12], J7.pin2
  N15: U1.PB5_(SCK/PCINT5)_[D13], J7.pin3, J9.pin3
  N16: U1.AVCC, J3.pin8
  N17: U1.GND#21, J4.pin8
  N18: J1.pin1, J2.pin1, J4.pin1
  N19: J1.pin2, R1.Pin_0
  N20: J1.pin3, R4.Pin_0, R5.Pin_0
  N21: J1.pin4, J3.pin1, J5.pin1
  N22: J2.pin7, C4.0
  N23: J2.pin8, C3.0
  N24: J3.pin5, U2.output_voltage, C5.-
  N25: J4.pin2, J9.pin1
  N26: J4.pin3, C6.-
  N27: J4.pin4, C5.+
  N28: J4.pin5, U2.input_voltage
  N29: J4.pin6, D1.anode
  N30: J4.pin7, D2.anode
  N31: J5.pin7, R3.Pin_0
  N32: J8.pin1, U2.GND, C6.+

notes:
  Vcc
  GND
  VCC
  GND
  VCC CSN MOSI IRQ
  GND CE SCK MISO
  INPUT OUTPUT GND

custom parts:
  ATmega 328P: Atmel ATmega 328P-PU Microcontroller
  Ceramic Capacitor: 100 nF multilayer Ceramic Capacitor
